// Logisim project Main.circ as structural Verilog
module registerBank (
  input  in_1,
  input  in_2
);

  Register #(.width(12)) AR ();  // open: D, en, Q, clk, clr
  Register #(.width(12)) PC ();  // open: D, en, Q, clk, clr
  Register #(.width(12)) SP ();  // open: D, en, Q, clk, clr
  Register #(.width(16)) RR ();  // open: D, en, Q, clk, clr
  Register #(.width(16)) IR ();  // open: D, en, Q, clk, clr
  Register #(.width(16)) IR_2 ();  // open: D, en, Q, clk, clr
  RAM #(.addrWidth(12), .dataWidth(16)) ram_1 ();  // open: addr, data, sel, clk, ld, clr
endmodule
